# Fritzing sketch Project 2 fritz (saved by Fritzing 0.9.3b)
breadboards: 1

parts:
  GLCD_128x1 = 128 x 64 Graphic LCD
  Raspberry_Pi_1 = Raspberry Pi 3 [part_number=RPI-3-V1.2]  # not connected
  R1 = TRIMPOT [package=trimpot_pth_s3_lock]
  M1 = Dagu DGServo 9g (Top view) [part_number=RS001B]
  R2 = Resistor [tolerance=±5% resistance=1k package="0402 [SMD]"]
  S2 = Pushbutton [package=THT]
  Part1 = Adafruit DC+Stepper Motor HAT [part_number="Adafruit #2348"]
  J1 = T Cobbler Plus
  M2 = DC Motor
  M3 = DC Motor
  BAT2 = Battery Holders [package=battery-aa-panel]  # not connected
  BAT3 = Battery Holders [package=battery-aa-panel]
  BAT4 = Battery Holders [package=battery-aa-panel]  # not connected
  BAT5 = Battery Holders [package=battery-aa-panel]  # not connected
  BAT6 = Battery Holders [package=battery-aa-panel]

nets:
  N1: GLCD_128x1.1_Vss, GLCD_128x1.20_K(-), R1.CCW, J1.GND#13
  N2: GLCD_128x1.2_Vdd, R1.CW, J1.5.0V#3
  N3: GLCD_128x1.3_Vo, R1.WIPER
  N4: GLCD_128x1.4_D/I, J1.CE1
  N5: GLCD_128x1.5_R/W, J1.MOSI
  N6: GLCD_128x1.6_Enable, J1.SCLK
  VCC: GLCD_128x1.19_A(+), M1.vcc, R2.Pin_1, J1.3.3V
  N7: M1.gnd, S2.leg1, J1.GND#8
  N8: S2.leg0, J1.#5
  N9: Part1.M1B, M2.pin_1
  N10: Part1.M1A, M2.pin_2
  N11: Part1.M4A, M3.pin_1
  N12: Part1.M4B, M3.pin_2
  N13: Part1.GND, BAT3.+
  N14: Part1.VMOTOR, BAT6.-

notes:
  1.5V AAA Batteries x 5
  ST7920 128 x 64 LCD
  DFRobot DC Motor x 2
  Servo motor to hold catapult down
  Push button to control servo

custom parts:
  Adafruit DC+Stepper Motor HAT: Let your robotic dreams come true with the new DC+Stepper Motor HAT from Adafruit. This Raspberry Pi add-on is perfect for any motion project as it can drive up to 4 DC or 2 Stepper motors with full PWM speed control. Since the Raspberry Pi does not have a lot of PWM pins, we use a fully-dedicated PWM driver chip onboard to both control motor direction and speed. This chip handles all the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
  T Cobbler Plus: The T-Cobbler Plus is an add on prototyping board from Adafruit specifically designed for the Raspberry Pi B+ that can break out all those tasty power, GPIO, I2C and SPI pins from the 40-pin header onto a solderless breadboard. This set will make "cobbling together" prototypes with the Pi super easy. The T-Cobbler Plus can plug into any solderless breadboard.
